# Fritzing sketch microduino-bluetooth (saved by Fritzing 0.8.7b)
circuit board: 8.46667cm x 5.64444cm
breadboards: 1

parts:
  Componente1 = Bluetooth HC-05 Macho
  Microduino1 = Microduino-Core+
  Componente2 = Digital Temperature Sensor Breakout - TMP102

nets:
  N1: Componente1.TXD, Microduino1.D2
  N2: Componente1.RXD, Microduino1.D3
  VCC: Componente1.VCC, Microduino1.5V
  GND: Componente1.GND, Microduino1.GND, Componente2.GND
  N3: Microduino1.3V3, Componente2.V+
  N4: Microduino1.SDA, Componente2.SDA
  N5: Microduino1.SCL, Componente2.SCL

custom parts:
  Microduino-Core+: The awesome Arduino compatible microcontroller
