# Fritzing sketch microduino-debug (saved by Fritzing 0.9.2b)
circuit board: 8.46667cm x 5.64444cm

parts:
  Microduino_core+ = Microduino-Core+
  J1 = AVR ISP 6 Pin [package=2x3_lock]
  JP1 = Header 5x2 [package=avr_icsp]
  S1 = Toggle Switch [package=THT]

nets:
  N1: Microduino_core+.GND, J1.6, JP1.2
  N2: Microduino_core+.D13, J1.3
  N3: Microduino_core+.D12, J1.1
  N4: Microduino_core+.D11, J1.4
  N5: Microduino_core+.RST, J1.5, JP1.6
  N6: Microduino_core+.3V3, S1.L2
  N7: Microduino_core+.5V, S1.L1
  N8: Microduino_core+.D16, JP1.9
  N9: Microduino_core+.D17, JP1.3
  N10: Microduino_core+.D18, JP1.5
  N11: Microduino_core+.D19, JP1.1
  N12: J1.2, JP1.4, S1.COM

custom parts:
  Microduino-Core+: The awesome Arduino compatible microcontroller
