# Fritzing sketch global (saved by Fritzing 1.0.5)
circuit board: 10.8288cm x 7.59468cm

parts:
  WeMos_D1_Mini_Micro_SD_Shield1 = WeMos D1 Mini Micro SD Shield
  WeMos_D1_Mini_OLED_Shield1 = WeMos D1 Mini OLED Shield
  WeMos_D1_Mini1 = WeMos D1 Mini
  SHT85 = SHT85 Temperature and Humdity Sensor [package=sht85]
  SPS30 = SPS30 [package=1x05-1mm]
  SCD30 = SCD30
  GPS = waveshare LC78G
  StimaWifi_D1_connection_board = StimaWifi D1 connection board

nets:
  3V3: WeMos_D1_Mini_Micro_SD_Shield1.3V3, WeMos_D1_Mini_OLED_Shield1.3V3, WeMos_D1_Mini1.3V3, SHT85.VDD, SCD30.VDD, StimaWifi_D1_connection_board.3V3, StimaWifi_D1_connection_board.3v3
  5V: WeMos_D1_Mini_Micro_SD_Shield1.5V, WeMos_D1_Mini_OLED_Shield1.5V, WeMos_D1_Mini1.5V, SPS30.VDD, GPS.VCC, StimaWifi_D1_connection_board.5V
  N1: WeMos_D1_Mini_Micro_SD_Shield1.A0, WeMos_D1_Mini_OLED_Shield1.A0, WeMos_D1_Mini1.A0, StimaWifi_D1_connection_board.A0
  N2: WeMos_D1_Mini_Micro_SD_Shield1.D0, WeMos_D1_Mini_OLED_Shield1.D0, WeMos_D1_Mini1.D0, StimaWifi_D1_connection_board.D0
  N3: WeMos_D1_Mini_Micro_SD_Shield1.D1, WeMos_D1_Mini_OLED_Shield1.D1, WeMos_D1_Mini1.D1, SHT85.SCK, SPS30.SCL, SCD30.TX/SCL, StimaWifi_D1_connection_board.D1, StimaWifi_D1_connection_board.SCL
  N4: WeMos_D1_Mini_Micro_SD_Shield1.D2, WeMos_D1_Mini_OLED_Shield1.D2, WeMos_D1_Mini1.D2, SHT85.SDA, SPS30.SDA, SCD30.RX/SDA, StimaWifi_D1_connection_board.D2, StimaWifi_D1_connection_board.SDA
  N5: WeMos_D1_Mini_Micro_SD_Shield1.D3, WeMos_D1_Mini_OLED_Shield1.D3, WeMos_D1_Mini1.D3, StimaWifi_D1_connection_board.D3
  N6: WeMos_D1_Mini_Micro_SD_Shield1.D4, WeMos_D1_Mini_OLED_Shield1.D4, WeMos_D1_Mini1.D4, StimaWifi_D1_connection_board.D4
  N7: WeMos_D1_Mini_Micro_SD_Shield1.D5, WeMos_D1_Mini_OLED_Shield1.D5, WeMos_D1_Mini1.D5, StimaWifi_D1_connection_board.D5
  N8: WeMos_D1_Mini_Micro_SD_Shield1.D6, WeMos_D1_Mini_OLED_Shield1.D6, WeMos_D1_Mini1.D6, StimaWifi_D1_connection_board.D6
  N9: WeMos_D1_Mini_Micro_SD_Shield1.D7, WeMos_D1_Mini_OLED_Shield1.D7, WeMos_D1_Mini1.D7, StimaWifi_D1_connection_board.D7
  N10: WeMos_D1_Mini_Micro_SD_Shield1.D8, WeMos_D1_Mini_OLED_Shield1.D8, WeMos_D1_Mini1.D8, StimaWifi_D1_connection_board.D8
  N11: WeMos_D1_Mini_Micro_SD_Shield1.G, WeMos_D1_Mini_OLED_Shield1.G, WeMos_D1_Mini1.G
  N12: WeMos_D1_Mini_Micro_SD_Shield1.RST, WeMos_D1_Mini_OLED_Shield1.RST, WeMos_D1_Mini1.RST, StimaWifi_D1_connection_board.RST
  N13: WeMos_D1_Mini_Micro_SD_Shield1.RX, WeMos_D1_Mini_OLED_Shield1.RX, WeMos_D1_Mini1.RX, GPS.TX-O, StimaWifi_D1_connection_board.RX, StimaWifi_D1_connection_board.B
  N14: WeMos_D1_Mini_Micro_SD_Shield1.TX, WeMos_D1_Mini_OLED_Shield1.TX, WeMos_D1_Mini1.TX, GPS.RX-I, StimaWifi_D1_connection_board.TX, StimaWifi_D1_connection_board.A
  GND: SHT85.GND, SPS30.SEL, SPS30.GND, SCD30.GND, GPS.GND, StimaWifi_D1_connection_board.G, StimaWifi_D1_connection_board.GND

custom parts:
  SHT85 Temperature and Humdity Sensor: SHT1x Humdity Sensor Sensirion humdity sensor. Schematic element and footprint proven. Spark Fun Electronics SKU : COM-08227
  SPS30: Header 5 Standard 5-pin 0.1 header. Use with straight break away headers (SKU : PRT-00116), right angle break away headers (PRT-00553), swiss pins (PRT-00743), machine pins (PRT-00117), and female headers (PRT-00115). Molex polarized connector foot print use with SKU : PRT-08230 with associated crimp pins and housings.
  SCD30: CO2 , humidity, and temperature sensor * Current consumption: 19 mA @ 1 meas. per 2 s. * Digital interface UART or I2C * Company: Sensirion - The Sensor Company Electrical specifications * average current: 19 mA * max. current: 75 mA * DC supply: 3.3 V - 5.5 V Operation conditions * temperature: 0 – 50°C * humidity: 0 – 95 %RH * sensor lifetime: 15 years CO2-sensor: * NDIR CO 2 sensor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
